// Logisim project f1.circ as structural Verilog: 1 circuit, main circuit main
module main (
  input  in_1,
  input  in_2,
  input  in_3,
  input  in_4,
  input  in_5,
  input  in_6,
  input  in_7,
  input  in_8,
  input  in_9,
  input  in_10,
  input  in_11,
  output out_12,
  output out_13,
  output out_14,
  output out_15,
  output out_16,
  output out_17
);

  wire and_2_out, or_2_out;

  and and_1 (out_12, in_1, in_3);
  or or_1 (out_14, in_5, in_7);
  not not_1 (out_17, in_11);
  and and_2 (and_2_out, in_2, in_4);
  or or_2 (or_2_out, in_6, in_8);
  xor xor_1 (out_16, in_9, in_10);
  not not_2 (out_13, and_2_out);
  not not_3 (out_15, or_2_out);

  // Notes on the sheet:
  //   A.B
  //   A+B
  //   'A
  //   '(A.B)
  //   '(A+B)
endmodule
